# Fritzing sketch Arduino_Assignment2 (saved by Fritzing 0.9.4)
breadboards: 1

parts:
  Part1 = Arduino Uno (Rev3)
  S1 = Pushbutton [package="[THT]"]
  S2 = Pushbutton [package="[THT]"]
  S3 = Pushbutton [package="[THT]"]
  S4 = Pushbutton [package="[THT]"]
  R1 = Resistor [tolerance=±5% resistance=220 package=THT]
  R2 = Resistor [tolerance=±5% resistance=220 package=THT]
  R3 = Resistor [tolerance=±5% resistance=220 package=THT]
  R4 = Resistor [tolerance=±5% resistance=220 package=THT]
  U1 = POT [package=alps_pot]
  U2 = Vibration Motor- ROB-08449 [package=vibe-motor-10mm]
  Q1 = MOSFET-NCHANNEL [package=to220v]
  R5 = Resistor [tolerance=±5% resistance=220 package=THT]
  D1 = Diode [package=diode-hv]

nets:
  N1: Part1.A0, U1.S
  N2: Part1.D13/SCK, R5.Pin_0
  N3: Part1.D2, S4.Pin_1, S4.Pin_2, R3.Pin_0
  N4: Part1.D3_PWM, S3.Pin_1, S3.Pin_2, R4.Pin_0
  N5: Part1.D4, S2.Pin_1, S2.Pin_2, R2.Pin_0
  N6: Part1.D5_PWM, S1.Pin_1, S1.Pin_2, R1.Pin_0
  N7: Part1.5V, S1.Pin_3, S1.Pin_4, S2.Pin_3, S2.Pin_4, S3.Pin_3, S3.Pin_4, S4.Pin_3, S4.Pin_4, U1.E, U2.-
  N8: Part1.GND, R1.Pin_1, R2.Pin_1, R3.Pin_1, R4.Pin_1, U1.A, Q1.S, D1.C
  N9: U2.+, Q1.D
  N10: Q1.G, R5.Pin_1
